# Fritzing sketch scheme2_with_sound (saved by Fritzing 0.9.9b)

parts:
  Компонент1 = Arduino Nano (Rev3.0)
  Компонент2 = InvenSense MPU6050
  Компонент4 = Adafruit MicroLipo Charger USB Type C [part_number="Adafruit #4410"]
  U2 = LIPO-110mAh [package=lipo-110]
  S1 = Toggle Switch [package=THT]
  S2 = Pushbutton [package="[SMD]"]
  S3 = Pushbutton [package="[SMD]"]
  8x8_LED_Modul_mit_MAX1 = 8x8 LED Modul mit MAX7219 [package=THT]
  8x8_LED_Modul_mit_MAX2 = 8x8 LED Modul mit MAX7219 [package=THT]
  J1 = Piezo Speaker

nets:
  GND: Компонент1.GND, Компонент2.GND, Компонент4.GND, U2.-, S2.Pin_3, S2.Pin_4, S3.Pin_1, S3.Pin_2, 8x8_LED_Modul_mit_MAX1.GND_Eingang, J1.pin1
  N1: Компонент1.D2, S3.Pin_3, S3.Pin_4
  N2: Компонент1.D3, S2.Pin_1, S2.Pin_2
  N3: Компонент1.D4, 8x8_LED_Modul_mit_MAX1.DIN_Eingang
  N4: Компонент1.D5, 8x8_LED_Modul_mit_MAX1.CLK_Eingang
  N5: Компонент1.D6, 8x8_LED_Modul_mit_MAX1.CS_Eingang
  N6: Компонент1.D9, J1.pin2
  5V: Компонент1.5V, Компонент2.VCC, S1.L1, 8x8_LED_Modul_mit_MAX1.VCC_Eingang
  N7: Компонент1.A5, Компонент2.SCL
  N8: Компонент1.A4, Компонент2.SDA
  N9: Компонент4.VBAT, U2.+
  N10: Компонент4.5V, S1.COM
  N11: 8x8_LED_Modul_mit_MAX1.VCC_Ausgang, 8x8_LED_Modul_mit_MAX2.VCC_Eingang
  N12: 8x8_LED_Modul_mit_MAX1.GND_Ausgang, 8x8_LED_Modul_mit_MAX2.GND_Eingang
  N13: 8x8_LED_Modul_mit_MAX1.DOUT_Ausgang, 8x8_LED_Modul_mit_MAX2.DIN_Eingang
  N14: 8x8_LED_Modul_mit_MAX1.CS_Ausgang, 8x8_LED_Modul_mit_MAX2.CS_Eingang
  N15: 8x8_LED_Modul_mit_MAX1.CLK_Ausgang, 8x8_LED_Modul_mit_MAX2.CLK_Eingang

custom parts:
  Adafruit MicroLipo Charger USB Type C: Oh so handy, this little lipo charger is so small and easy to use you can keep it on your desk or mount it easily into any project! Simply plug it via any USB C cable into a USB port and a 3.7V/4.2V lithium polymer or lithium ion rechargeable battery into the JST plug on the other end. There are two LEDs - one red and one green. While charging, the red LED is lit. When the battery is fully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
